# Fritzing sketch Sterownik (saved by Fritzing 0.8.5b)
circuit board: 13.0177cm x 8.76233cm
breadboards: 1

parts:
  R1 = Resistor [tolerance=±5% resistance=220 package=THT]
  LCD1 = LCD screen
  S1 = Pushbutton [package="[THT]"]
  R5 = Resistor [tolerance=±5% resistance=4.7k package=THT]
  R6 = Resistor [tolerance=±5% resistance=4.7k package=THT]
  R4 = Rotary Potentiometer (Small) [maximum_resistance=100kΩ package=THT]
  Arduino = Arduino Pro Mini v13
  RTC1 = DS1307 RTC Breakout

nets:
  N1: R1.Pin_0, Arduino.D2
  VDD: R1.Pin_1, LCD1.VDD, S1.Pin_1, S1.Pin_2, R5.Pin_1, R6.Pin_1, R4.leg2, Arduino.VCC, RTC1.5V
  GND: LCD1.VSS, LCD1.R/W, LCD1.LED-, R4.leg1, Arduino.GND, RTC1.GND
  N2: LCD1.V0, R4.wiper
  N3: LCD1.RS, Arduino.D4
  N4: LCD1.E, Arduino.D5_PWM
  N5: LCD1.DB0, Arduino.D6_PWM
  N6: LCD1.DB1, Arduino.D7
  N7: LCD1.DB2, Arduino.D8
  N8: LCD1.DB3, Arduino.D9_PWM
  N9: LCD1.DB4, Arduino.D10_PWM/SS
  N10: LCD1.DB5, Arduino.D11_PWM/MOSI
  N11: LCD1.DB6, Arduino.D12/MISO
  N12: LCD1.DB7, Arduino.D13/SCK
  N13: LCD1.LED+, S1.Pin_3, S1.Pin_4
  N14: R5.Pin_0, Arduino.A4, RTC1.SCL
  N15: R6.Pin_0, Arduino.A5, RTC1.SDA

notes:
  1-Wire
  I2C
  GND

custom parts:
  DS1307 RTC Breakout: DS1307 Real-time Clock Breakout Board with Battery
